# Fritzing sketch bidirectional_people_counter_diagram (saved by Fritzing 0.9.3b)

parts:
  A1 = MH-ET Live Minikit for ESP32
  M1 = E18-D80NK_1 [package=THT]
  LED1 = LED - 5mm [color="Red (633nm)" package="5 mm [THT]"]
  LED2 = LED - 5mm [color="Green (565nm)" package="5 mm [THT]"]
  R1 = Resistor [tolerance=±5% resistance=220 package=THT]
  R2 = Resistor [tolerance=±5% resistance=220 package=THT]
  S1 = Pushbutton [package="[THT]"]
  M2 = E18-D80NK_1 [package=THT]

nets:
  N1: A1.IO5, M1.pin3
  N2: A1.IO17, R1.Pin_0
  N3: A1.IO16, R2.Pin_0
  N4: A1.GND, M1.pin1, LED1.cathode, LED2.cathode, S1.Pin_4, M2.pin1
  N5: A1.VCC, M1.pin2, M2.pin2
  N6: A1.IO27, S1.Pin_2
  N7: A1.IO4, M2.pin3
  N8: LED1.anode, R1.Pin_1
  N9: LED2.anode, R2.Pin_1

custom parts:
  MH-ET Live Minikit for ESP32: MH-ET Live Minikit for ESP32 ( http://mh.nodebb.com/topic/8/mh-et-live-minikit-for-esp32/2/) PCB footprint is invalid.
  E18-D80NK_1: E18-D80NK Proximity Sensor module.
